// Digital circuit atk16.dig as structural Verilog
module atk16 (
  input  IN,
  input  clk,
  output OUT
);

  wire ALU_OE, atk16_ucode_addr_1_int_active, FR_IE, IM_DS, IM_EN, IM_M, IPC_IE, IPC_OE, IR_IE, ISRA_OE,
       keyboard_1_av, LI_OE, MAR_IE, MEM_IE, MEM_OE, not_1_out, or_1_out, PC_CO, PC_IE, PC_OE, R1_OE, R2_OE,
       reset_1_out, RW_IE, US_RS;
  wire [1:0] IT_N;
  wire [2:0] atk16_decoder_1_alu_s, atk16_decoder_1_r1_s, atk16_decoder_1_r2_s, FLAG_S, US_Q;
  wire [3:0] ALU_flags, FR_Q, OPCODE;
  wire [3:3] rs_ff_as_1_q;
  wire [7:0] atk16_ucode_addr_1_addr;
  wire [15:0] ALU_y, atk16_alu_inputs_1_a, atk16_alu_inputs_1_b, atk16_jump_unit_1_pc_res,
       atk16_regbank_1_d1, atk16_regbank_1_d2, driver_1_out, IPC_q, MAR_q, PC_out;
  wire [23:14] UCODE_d;

  Register #(.Bits(16)) IPC (.D(driver_1_out), .C(clk), .en(IPC_IE), .Q(IPC_q));
  assign driver_1_out = IPC_OE ? IPC_q : 16'bz;  // Driver driver_1
  assign driver_1_out = ISRA_OE ? {14'h4, IT_N} : 16'bz;  // Driver driver_2
  atk16_decoder atk16_decoder_1 (
    .DBUS(driver_1_out), .IR_IE(IR_IE), .CLK(clk), .LI_OE(LI_OE), .OP(OPCODE), .RW_S(FLAG_S),
    .ALU_S(atk16_decoder_1_alu_s), .R1_S(atk16_decoder_1_r1_s), .R2_S(atk16_decoder_1_r2_s));
  Reset #(.invertOutput("false")) reset_1 (.out(reset_1_out));
  atk16_jump_unit atk16_jump_unit_1 (.ADDR(driver_1_out), .PC(PC_out), .IM_M(IM_M), .PC_RES(atk16_jump_unit_1_pc_res));
  not not_1 (not_1_out, clk);
  or or_1 (or_1_out, US_RS, reset_1_out);
  Keyboard keyboard_1 (.C(clk), .en(1'b1), .av(keyboard_1_av));  // open: D
  Counter #(.Bits(3)) Microsequencer (.en(1'b1), .C(not_1_out), .clr(or_1_out), .out(US_Q));  // open: ovf
  RS_FF_AS rs_ff_as_1 (.S(keyboard_1_av), .R(IM_DS), .Q(rs_ff_as_1_q[3]));  // open: nQ
  CounterPreset #(.Bits(16), .isProgramCounter("true")) PC (
    .en(PC_CO), .C(clk), .dir(1'b0), .in(atk16_jump_unit_1_pc_res), .ld(PC_IE), .clr(1'b0), .out(PC_out));  // open: ovf
  atk16_regbank atk16_regbank_1 (
    .Din(driver_1_out), .RW_IE(RW_IE), .RW_S(FLAG_S), .CLK(clk), .R1_S(atk16_decoder_1_r1_s),
    .R2_S(atk16_decoder_1_r2_s), .D1(atk16_regbank_1_d1), .D2(atk16_regbank_1_d2));
  assign driver_1_out = PC_OE ? PC_out : 16'bz;  // Driver driver_3
  atk16_ucode_addr atk16_ucode_addr_1 (
    .FLAG_S(FLAG_S), .FR_Q(FR_Q), .OP(OPCODE), .US_Q(US_Q), .IRQ({rs_ff_as_1_q[3], 3'b000}), .IM_EN(IM_EN),
    .IM_DS(IM_DS), .ADDR(atk16_ucode_addr_1_addr), .IT_N(IT_N), .INT_ACTIVE(atk16_ucode_addr_1_int_active));
  LED led_1 (.in(atk16_ucode_addr_1_int_active));
  // Probe OPCODE on OPCODE
  // Probe PC on PC_out
  // Probe Bus on driver_1_out
  assign driver_1_out = R1_OE ? atk16_regbank_1_d1 : 16'bz;  // Driver driver_4
  EEPROM #(.AddrBits(8), .Bits(24)) UCODE (
    .A(atk16_ucode_addr_1_addr), .CS(1'b1), .WE(1'b0), .OE(1'b1),
    .D({UCODE_d[23:21], IPC_OE, IPC_IE, IM_EN, IM_DS, ISRA_OE, US_RS, UCODE_d[14], FR_IE, ALU_OE, LI_OE, IM_M, IR_IE, R2_OE, R1_OE, RW_IE, MEM_OE, MEM_IE, MAR_IE, PC_OE, PC_IE, PC_CO}));
  assign driver_1_out = R2_OE ? atk16_regbank_1_d2 : 16'bz;  // Driver driver_5
  atk16_alu_inputs atk16_alu_inputs_1 (
    .R1(atk16_regbank_1_d1), .R2(atk16_regbank_1_d2), .R2_S(atk16_decoder_1_r2_s), .IM_M(IM_M),
    .A(atk16_alu_inputs_1_a), .B(atk16_alu_inputs_1_b));
  Register #(.Bits(16)) MAR (.D(driver_1_out), .C(clk), .en(MAR_IE), .Q(MAR_q));
  atk16_alu ALU (
    .A(atk16_alu_inputs_1_a), .B(atk16_alu_inputs_1_b), .S(atk16_decoder_1_alu_s), .Y(ALU_y),
    .FLAGS(ALU_flags));
  Stop stop_1 (.stop(UCODE_d[14]));
  atk16_mem atk16_mem_1 (.ADDR(MAR_q), .DBUS(driver_1_out), .MEM_IE(MEM_IE), .MEM_OE(MEM_OE));
  Break break_1 (.brk(clk));
  assign driver_1_out = ALU_OE ? ALU_y : 16'bz;  // Driver driver_6
  Register #(.Bits(4)) FR (.D(ALU_flags), .C(clk), .en(FR_IE), .Q(FR_Q));

  assign OUT = 1'b0;
  // also tied to GND on the sheet: IN

  // Notes on the sheet:
  //   OUT: Dummy output
  //   clk: Hz: 15
  //   contents of UCODE (hex, n*v repeats v):
  //   c,221,3040,8000,4*0,c,221,3040,8000,4*0,c,221,3440,8000,4*0,c
  //   ,221,3440,8000,4*0,c,221,88,60,8000,0,0,0,c,221,88,60,8000,0,0,0
  //   ,c,221,88,110,8000,0,0,0,c,221,88,110,8000,0,0,0,c,221,840,8000
  //   ,4*0,c,221,840,8000,4*0,c,221,82,8000,4*0,c,221,82,8000,4*0,c
  //   ,221,c02,8000,4*0,c,221,c02,8000,4*0,c,221,8000,5*0,c,221,82,8000
  //   ,4*0,c,221,8000,5*0,c,221,c02,8000,4*0,c,221,44,8000,4*0,c,221
  //   ,44,8000,4*0,c,221,8000,5*0,c,221,8000,5*0,c,221,8000,5*0,c,221
  //   ,8000,5*0,c0004,10008,22,8000,4*0,c0004,10008,22,8000,4*0,c0004
  //   ,10008,22,8000,4*0,c0004,10008,22,8000,4*0,c,221,120002,8000,4*0
  //   ,c,221,120002,8000,4*0,c,221,4000,5*0,c,221,4000
endmodule

/* Test case Sum program TODO:
IN OUT

program(0x4051, 0x40a2, 0x029b)

0 x
*/
