// Digital circuit atk16_ppu.dig as structural Verilog
module atk16_ppu (
  input  PCLK,
  input  CLK,
  output [8:0] SCANLINE
);

  wire comparator_1_gt, comparator_2_gt, comparator_3_gt, comparator_4_lt, comparator_5_gt, comparator_6_lt,
       HSYNC, PB, PG, PR, VSYNC;
  wire [0:0] SCAN_L2;
  wire [1:0] add_2_s;
  wire [3:3] multiplexer_1_out;
  wire [9:0] barrelshifter_1_out, barrelshifter_2_out, counter_1_out, counter_2_out;
  wire [15:0] VWORD_q;

  Counter #(.Bits(10)) counter_1 (.en(1'b1), .C(PCLK), .clr(comparator_1_gt), .out(counter_1_out));  // open: ovf
  Counter #(.Bits(10)) counter_2 (
    .en(1'b1), .C(comparator_1_gt), .clr(comparator_2_gt), .out(counter_2_out));  // open: ovf
  BarrelShifter #(.Bits(10), .direction("right")) barrelshifter_1 (
    .in(counter_2_out), .shift(4'b0001), .out(barrelshifter_1_out));
  BarrelShifter #(.Bits(10), .direction("right")) barrelshifter_2 (
    .in(counter_1_out), .shift(4'b0001), .out(barrelshifter_2_out));
  Comparator #(.Bits(10)) comparator_1 (.a(counter_1_out), .b(10'h31e), .gt(comparator_1_gt));  // open: eq, lt
  Comparator #(.Bits(10)) comparator_2 (.a(counter_2_out), .b(10'h20b), .gt(comparator_2_gt));  // open: eq, lt
  Comparator #(.Bits(10)) comparator_3 (.a(counter_2_out), .b(10'h1e8), .gt(comparator_3_gt));  // open: eq, lt
  Comparator #(.Bits(10)) comparator_4 (.a(counter_2_out), .b(10'h1eb), .lt(comparator_4_lt));  // open: gt, eq
  Add #(.Bits(10)) add_1 (.a(barrelshifter_1_out), .b(10'h1), .c_i(1'b0), .s({SCANLINE, SCAN_L2[0]}));  // open: c_o
  Register #(.Bits(16)) VWORD (.D(16'h421f), .C(CLK), .en(1'b1), .Q(VWORD_q));
  nand nand_1 (VSYNC, comparator_3_gt, comparator_4_lt);
  Add #(.Bits(2)) add_2 (
    .a({SCANLINE[0], SCAN_L2[0]}), .b(barrelshifter_2_out[1:0]), .c_i(1'b0), .s(add_2_s));  // open: c_o
  Comparator #(.Bits(10)) comparator_5 (.a(counter_1_out), .b(10'h28e), .gt(comparator_5_gt));  // open: eq, lt
  Comparator #(.Bits(10)) comparator_6 (.a(counter_1_out), .b(10'h2ef), .lt(comparator_6_lt));  // open: gt, eq
  Multiplexer #(.Selector_Bits(2), .Bits(4)) multiplexer_1 (
    .sel(add_2_s), .in_0(VWORD_q[3:0]), .in_1(VWORD_q[7:4]), .in_2(VWORD_q[11:8]), .in_3(VWORD_q[15:12]),
    .out({multiplexer_1_out[3], PR, PG, PB}));
  nand nand_2 (HSYNC, comparator_5_gt, comparator_6_lt);
  VGA vga_1 (.R(PR), .G(PG), .B(PB), .H(HSYNC), .V(VSYNC), .C(PCLK));

  // Other names for the same wires on the sheet: SCAN_L2[1] = SCANLINE[0]

  // Notes on the sheet:
  //   PCLK: Pixel clock
  //   CLK: CPU clock
  //   SCANLINE: Index of next scanline
endmodule
