// Digital circuit atk16_tpu.dig as structural Verilog
module atk16_tpu (
  input  [12:0] MMIO_S,
  input  MMIO_IE,
  input  MMIO_OE,
  input  PCLK,
  input  CLK,
  input  [15:0] DBUS,
  input  [8:0] X,
  input  [7:0] Y,
  output [1:0] PR,
  output [1:0] PG,
  output [1:0] PB
);

  wire COVF, not_1_out;
  wire [2:0] CX;
  wire [5:0] TX;
  wire [7:0] CHAR_S, CHARMEM_d;

  not not_1 (not_1_out, COVF);
  RAMDualPort #(.AddrBits(11), .Bits(8)) TEXTMEM (
    .A({TX, Y[7:3]}), .Din({8{1'b0}}), .str(1'b0), .C(not_1_out), .ld(1'b1), .D(CHAR_S));
  Counter #(.Bits(3)) counter_1 (.en(1'b1), .C(PCLK), .clr(COVF), .out(CX));  // open: ovf
  Counter #(.Bits(6)) counter_2 (.en(1'b1), .C(COVF), .clr(1'b0), .out(TX));  // open: ovf
  // Probe on CHAR_S
  and and_1 (COVF, ~CX[0], ~CX[1], CX[2]);  // And
  EEPROM #(.AddrBits(11), .Bits(8)) CHARMEM (.A({CHAR_S, Y[2:0]}), .CS(1'b1), .WE(1'b0), .OE(1'b1), .D(CHARMEM_d));
  // Probe on CHARMEM_d
  BitSelector #(.Selector_Bits(3)) bitselector_1 (.in(CHARMEM_d), .sel(CX), .out(PB[1]));
  // Probe on CX
  // Probe on PB[1]

  assign PB[0] = PB[1];
  assign PG = {2{PB[1]}};
  assign PR = {2{PB[1]}};

  // Other names for the same wires on the sheet: CCOLOR = PB[1]; CY[2:0] = Y[2:0]; TY[4:0] = Y[7:3]

  // Notes on the sheet:
  //   MMIO_S: MMI/O selector
  //   PCLK: Pixel clock
  //   CLK: CPU clock
  //   DBUS: Data bus
  //   X: X pixel
  //   Y: Y pixel
  //   contents of CHARMEM (hex, n*v repeats v):
  //   6,9,9,f,9,9,9,0,3,5,5,7,9,9,f,0,6,9,1,1,1,9,6,0,f,1,1,3,1,1,f
  //   ,0,f,1,1,3,1,1,1,0,6,9,1,1,d,9,6,0,9,9,f,4*9,0,7,5*2,7,0,e,4*8
  //   ,9,6,0,9,5,3,5,5,9,9,0,6*1,f,0,9,f,f,4*9,0,9,b,b,d,d,9,9,0,6,5*9
  //   ,6,0,7,9,9,7,1,1,1,0,6,9,9,9,d,e,8,0,7,9,9,7,3,5,9,0,6,9,1,6,8
  //   ,9,6,0,7,6*2,0,6*9,e,0,6*9,6,0,4*9,f,f,9,0,9,9,6,4*9,0,9,9,9,e
  //   ,8,9,e,0,f,8,8,4,2,1,f
endmodule
